# Fritzing sketch VNB - Servo Tester - Circuit (saved by Fritzing 0.9.2b)

parts:
  JACK1 = 2.1mm Barrel Jack with Terminal Block
  Part3 = Arduino Prototyping Shield
  SERVO1 = Adafruit Feedback Servo (small)
  J1 = female pin header, 10 pins [form="♀ (female)"]  # not connected
  J2 = female pin header, 8 pins [form="♀ (female)"]
  J4 = female pin header, 8 pins [form="♀ (female)"]
  J3 = female pin header, 6 pins [form="♀ (female)"]

nets:
  N1: JACK1.POS, Part3.N$76, SERVO1.Power
  N2: JACK1.NEG, Part3.GND, SERVO1.Ground, J4.pin6, J4.pin7
  N3: Part3.A0, SERVO1.Feedback, J3.pin1
  N4: Part3.A1, J3.pin2
  N5: Part3.A2, J3.pin3
  N6: Part3.A3, J3.pin4
  N7: Part3.A4, J3.pin5
  N8: Part3.A5, J3.pin6
  N9: Part3.D0(RX), J2.pin8
  N10: Part3.D1(TX), J2.pin7
  N11: Part3.D2, J2.pin6
  N12: Part3.D3, J2.pin5
  N13: Part3.D4, J2.pin4
  N14: Part3.D5, SERVO1.Signal, J2.pin3
  N15: Part3.D6, J2.pin2
  N16: Part3.D7, J2.pin1
  N17: Part3.IOREF, J4.pin1, J4.pin2
  N18: Part3.RESET, J4.pin3
  N19: Part3.3.3V, J4.pin4
  N20: Part3.+5V, J4.pin5
  N21: Part3.+9V, J4.pin8

custom parts:
  Adafruit Feedback Servo (small): Adafruit Feedback Servo (Small)
